# Fritzing sketch Rangkaian (saved by Fritzing 0.9.3b)

parts:
  Part2 = RFID-RC522-v2
  Part1 = Arduino Uno (Rev3) - ICSP
  Part3 = Lilypad Battery Connect
  KY-1 = Keyes Relay [package=THT]
  J1 = Piezo Speaker
  L1 = Solenoid
  LED1 = LED - 3mm [color="Red (633nm)" package="3 mm [THT]"]
  LED2 = LED - 3mm [color="Green (570nm)" package="3 mm [THT]"]  # not connected
  R1 = Resistor [tolerance=±5% resistance=220 package="1206 [SMD]"]
  R2 = Resistor [tolerance=±5% resistance=220 package="1206 [SMD]"]
  7_Segment1 = 7 Segment Display  # not connected

nets (from the schematic view):
  N1: Part2.SDA, Part1.D10_PWM/SS
  N2: Part2.SCK, Part2.MISO, Part1.D12/MISO, Part1.D13/SCK
  N3: Part2.MOSI, Part1.D11_PWM/MOSI
  GND: Part2.GND, Part1.GND, KY-1.ground, LED1.cathode
  N4: Part2.RST, Part1.D9_PWM
  N5: Part2.3_3V, Part1.3V3
  N6: Part1.D2, KY-1.signal
  N7: Part1.D3_PWM, J1.pin2
  N8: Part1.D4, R2.Pin_1
  N9: Part1.D5_PWM, R1.Pin_1
  N10: Part1.5V, KY-1.power
  N11: Part3.-, KY-1.C
  N12: Part3.+, L1.pin2
  N13: KY-1.NC, L1.pin1

custom parts:
  RFID-RC522-v2: A simple China made RFID-RC522 Reader; do check the pin labels, as this is a MFRC522 based clone.
  Keyes Relay: The Keyes 5V relay module is suitable for SCM development, home appliance control. It uses a 5V~12V TIL control signal which can control DC / AC signal.
